# Fritzing sketch LCD Screen Setup (saved by Fritzing 0.9.3b)
breadboards: 1

parts:
  Part1 = Arduino Uno (Rev3)
  LCD1 = LCD screen
  R1 = Resistor [tolerance=±5% resistance=220 package=THT]
  R2 = Trimmer Potentiometer [maximum_resistance=10kΩ package=THT]

nets:
  N1: Part1.D11_PWM/MOSI, LCD1.E
  N2: Part1.D12/MISO, LCD1.RS
  N3: Part1.D2, LCD1.DB7
  N4: Part1.D3_PWM, LCD1.DB6
  N5: Part1.D4, LCD1.DB5
  N6: Part1.D5_PWM, LCD1.DB4
  5V: Part1.5V, LCD1.VDD, R1.Pin_0, R2.leg1
  GND: Part1.GND, LCD1.VSS, LCD1.R/W, LCD1.LED-, R2.leg2
  N7: LCD1.V0, R2.wiper
  N8: LCD1.DB0, LCD1.DB3
  N9: LCD1.LED+, R1.Pin_1

// code stored in the sketch: LCD Screen Schematic.ino
#include <LiquidCrystal.h>  // Include the LiquidCrystal library

LiquidCrystal lcd(12, 11, 5, 4, 3, 2);  // Which pins will be used

void setup() {  // Begin the startup sequence

}

void loop() {  									// Execute the following commands repeatedly

  lcd.setCursor(0,0);  					// Where to begin printing
  lcd.print("<<<          >>>"); // Print text
  delay(500); 									  // Wait .5 seconds
  lcd.clear();										// Clear the screen

  lcd.print("<<<   Ryan   >>>"); // All text within quotations can be changed
  delay(500);
  lcd.clear();

  lcd.print("<<<          >>>");
  delay(500);										// All delays can be changed
  lcd.clear();

  lcd.setCursor(0,1);
  lcd.print("<<<MustySquad>>>");
  delay(500);
  lcd.clear();
  
  lcd.print("<<<          >>>");
  delay(500);
  lcd.clear();
  
  lcd.setCursor(0,0);
  lcd.print("<<< Cyprien   >>>");
  delay(500);
  lcd.clear();
  
  lcd.print("<<<          >>>");
  delay(500);
  lcd.clear();

  lcd.setCursor(0,1);
  lcd.print("<<<MustySquad>>>");
  delay(500);
  lcd.clear();
  
  lcd.print("<<<          >>>");
  delay(500);
  lcd.clear();

  lcd.setCursor(0,0);
  lcd.print("<<<  Connel  >>>");
  delay(500);
  lcd.clear();
  
  lcd.print("<<<          >>>");
  delay(500);
  lcd.clear();

  lcd.setCursor(0,1);
  lcd.print("<<<MustySquad>>>");
  delay(500);
  lcd.clear();

} 																// Stop loop sequence; begin again
