# Fritzing sketch OV7670camera (saved by Fritzing 0.9.3b)

parts:
  Part1 = Arduino Uno (Rev3)
  U1 = OV7670 Camera [package=camera_sfv24r-2st_2]
  R1 = Resistor [tolerance=±5% resistance=220 package="0603 [SMD]"]
  R2 = Resistor [tolerance=±5% resistance=220 package=THT]
  R3 = Resistor [tolerance=±5% resistance=220 package=THT]

nets:
  N1: Part1.A0, U1.D0
  N2: Part1.A1, U1.D1
  N3: Part1.A2, U1.D2
  N4: Part1.A3, U1.D3
  N5: Part1.A4/SDA, R1.Pin_1
  N6: Part1.A5/SCL, R2.Pin_0
  N7: Part1.D10_PWM/SS, U1.HREF
  N8: Part1.D11_PWM/MOSI, R3.Pin_0
  N9: Part1.D2, U1.PCLK
  N10: Part1.D3_PWM, U1.VSYNC
  N11: Part1.D4, U1.D4
  N12: Part1.D5_PWM, U1.D5
  N13: Part1.D6_PWM, U1.D6
  N14: Part1.D7, U1.D7
  N15: Part1.RESET, U1.RESET
  3V3: Part1.3V3, U1.3V3
  GND: Part1.GND, U1.GND, U1.PWDN
  N16: U1.SIOC, R2.Pin_1
  N17: U1.SIDO, R1.Pin_0
  N18: U1.XCLK, R3.Pin_1

custom parts:
  OV7670 Camera: CMOS image sensor
